# Fritzing sketch Light Sensor (saved by Fritzing 0.9.3b)
breadboards: 1

parts:
  U1 = ESP8266-01S [part_number=ESP8266]
  Onderdeel1 = FTDI Basic Programmer
  C1 = Electrolytic Capacitor [capacitance=1µF package="100 mil [THT, electrolytic]"]
  S1 = Pushbutton [package="[THT]"]
  S2 = Pushbutton [package="[THT]"]
  R1 = Resistor [tolerance=±5% resistance=10k package=THT]
  R2 = Resistor [tolerance=±5% resistance=10k package=THT]
  R3 = Resistor [tolerance=±5% resistance=10k package=THT]
  R4 = Resistor [tolerance=±5% resistance=10k package=THT]
  R5 = Photocell (LDR) [package=THT]
  U2 = ESP8266-01S [part_number=ESP8266]  # not connected

nets:
  N1: U1.RXD, Onderdeel1.TXO
  N2: U1.VCC, Onderdeel1.POWER, C1.+, R1.Pin_1, R2.Pin_1, R3.Pin_1, R5.pin_1
  N3: U1.GPIO_0, S1.Pin_1, S1.Pin_2, R1.Pin_0
  N4: U1.RST, S2.Pin_1, S2.Pin_2, R2.Pin_0
  N5: U1.GPIO_2, R4.Pin_0, R5.pin_0
  N6: U1.CH_PD, R3.Pin_0
  GND: U1.GND, Onderdeel1.GND, C1.-, S1.Pin_3, S1.Pin_4, S2.Pin_3, S2.Pin_4, R4.Pin_1
  N7: U1.TXD, Onderdeel1.RXI

notes:
  PROGRAM
  RESET
  470μF ~ 3,6V
  https://www.studiopieters.nl
  VCC
  RST
  CH_PD
  TXD
  RXD
  GND
  GPIO2
  GPIO0

custom parts:
  FTDI Basic Programmer: Description: This is the newest revision of our FTDI Basic. We now use a SMD 6-pin header on the bottom, which makes it smaller and more compact. Functionality has remained the same. This is a basic breakout board for the FTDI FT232RL USB to serial IC. The pinout of this board matches the FTDI cable to work with official Arduino and cloned 3.3V Arduino boards. It can also be used for general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
